# Fritzing sketch Automatic Door (saved by Fritzing 0.9.3b)

parts:
  Part1 = ACS712 Low Current Sensor Board v12
  M2 = DC Motor
  KY-1 = Keyes Relay [package=THT]
  KY-2 = Keyes Relay [package=THT]
  KY-3 = Keyes Relay [package=THT]
  KY-4 = Keyes Relay [package=THT]
  J1 = Power Jack [package=power_jack_pth_lock]
  Part2 = Arduino Uno (Rev3) - ICSP
  S1 = SWITCH-MOMENTARY-2 [package=tactile-pth]
  R1 = Resistor [tolerance=±5% resistance=100k package="2512 [SMD]"]
  S2 = SWITCH-MOMENTARY-2 [package=tactile-pth]
  R2 = Resistor [tolerance=±5% resistance=100k package=THT]

nets:
  N1: Part1.IP+, M2.pin_1, KY-1.NO, KY-3.C, KY-4.C, KY-4.NO
  N2: Part1.IP-, J1.PWR, Part2.VIN
  5V: Part1.5V, KY-1.power, KY-2.power, KY-3.power, KY-4.power, Part2.5V
  N3: Part1.VO, Part2.A0
  GND: Part1.GND, KY-1.C, KY-2.C, J1.GND, Part2.GND, R1.Pin_0, R2.Pin_0
  N4: M2.pin_2, KY-2.NO, KY-3.NO
  N5: KY-1.signal, Part2.D4
  N6: KY-1.ground, KY-2.ground, KY-3.ground, KY-4.ground
  N7: KY-2.signal, Part2.D3_PWM
  N8: KY-3.signal, Part2.D2
  N9: KY-4.signal, Part2.D5_PWM
  N10: Part2.A1, S1.2, R1.Pin_1
  N11: Part2.A2, S2.2, R2.Pin_1
  N12: Part2.3V3, S1.1, S2.1

notes:
  Open Button
  Close Button

custom parts:
  Keyes Relay: The Keyes 5V relay module is suitable for SCM development, home appliance control. It uses a 5V~12V TIL control signal which can control DC / AC signal.
